# Fritzing sketch ShiftRegister (saved by Fritzing 0.9.3b)
breadboards: 1

parts:
  Teensy_3_1 = Teensy 3.1
  U1 = 74HC595 [package="DIP16 [THT]"]

nets:
  GND: Teensy_3_1.GND, U1.GND, U1.OE
  N1: U1.MR, U1.VCC
