# Fritzing sketch lab4 sketch (saved by Fritzing 0.9.3b)
breadboards: 1

parts:
  Teensy_3_2 = Teensy 3.1  # not connected
  S1 = Pushbutton [package="[THT]"]
  R1 = Resistor [tolerance=±5% resistance=220 package="0805 [SMD]"]
  R2 = Resistor [tolerance=±5% resistance=220 package="0805 [SMD]"]  # not connected
  R3 = Resistor [tolerance=±5% resistance=220 package="0805 [SMD]"]
  LED1 = RGB LED (com. cathode, rgb) [package="5 mm [THT]"]
  R4 = Resistor [tolerance=±5% resistance=10k package=THT]
  S2 = Pushbutton [package="[THT]"]

nets:
  N1: S1.Pin_1, S1.Pin_2, LED1.common_cathode, S2.Pin_1, S2.Pin_2
  N2: S1.Pin_3, S1.Pin_4
  N3: R1.Pin_1, LED1.red_anode
  N4: R3.Pin_1, LED1.blue_anode
  N5: R4.Pin_0, R4.Pin_1
  N6: S2.Pin_3, S2.Pin_4
